# Fritzing sketch Untitled Sketch (saved by Fritzing 0.9.5d)
breadboards: 2

parts:
  J1 = Basic Servo
  Power_plug1 = Power plug
  Mod1 = KY-019 5V Relay Module [package="Breakout board"]
  Mod2 = KY-019 5V Relay Module [package="Breakout board"]
  U2 = LuaNode32 / ESP32 [part_number=ESP32S-PIN30]
  HC-SR04_Sensor_1 = HC-SR04 Ultrasonic Distance Sensor
  A3 = TS-300B interface
  A4 = TS 300B sensor
  U3 = SWITCH-SPST-2 [package=switch-spst-vertical]
  M5 = ph-4502c [package=THT]
  USBTTL1 = Micro USB B Plug
  USBTTL2 = USB A Plug
  VCC1 = Battery
  WATER_PUMP1 = water pump/motor  # not connected
  J2 = 220v plug

nets:
  GND: J1.gnd, Mod2.-, U2.GND, HC-SR04_Sensor_1.GND, A3.Pin_1, A3.Pin_8, M5.pin4, M5.pin5
  VCC: J1.vcc, Mod2.+, U2.Vin, HC-SR04_Sensor_1.VCC, A3.Pin_4
  N1: J1.pulse, U2.D14
  N2: Power_plug1.GND, Mod1.NO, USBTTL2.usb
  N3: Power_plug1.VCC, Mod1.NC
  N4: Mod1.S, U3.P
  N5: Mod1.+, U3.O, VCC1.+
  N6: Mod1.-, VCC1.-
  N7: Mod1.Common, USBTTL1.usb
  N8: Mod2.S, U2.D27
  N9: Mod2.NO, J2.pin1
  N10: U2.VP, A3.Pin_2
  N11: U2.VN, M5.pin3
  N12: U2.D12, HC-SR04_Sensor_1.TRIG
  N13: U2.D13, HC-SR04_Sensor_1.ECHO
  N14: U2.3V3, M5.pin6
  N15: A3.Pin_5, A4.Pin_1
  N16: A3.Pin_6, A4.Pin_2
  N17: A3.Pin_7, A4.Pin_3

notes:
  Powerbank
  Adaptor 12V
  Steker AC

custom parts:
  KY-019 5V Relay Module: KY-019 5V Relay module, used to control AC circuits. (Special thanks to vanepp for fixing the PCB holes and other errors)
  LuaNode32 / ESP32: New Image for LuaNode32 DOIT ESP32 DEVKIT V1. Base parts from LuaNode32 / ESP32 ESP32 based LuaNode32 by G.Noorlander DOIT Esp32 DevKit v1 (30 pins long, 11 pins width) by Werner Rothschopf (modified by vanepp Dec 2018)
  TS-300B interface: TS-300B interface.
  TS 300B sensor: TS 300B water turbidity sensor.
  ph-4502c: ph-4502c PH Meter.
  water pump/motor: WATER PUMP BY ARDUBLOCKTR
  220v plug: Generic 220V AC plug.
